// Logisim project cpu.circ as structural Verilog: 5 circuits, main circuit main
module main (
  input  Clock
);

  wire Reset_out;
  wire [15:0] programcounter_1_adress;

  Button Reset (.out(Reset_out));
  ProgramCounter programcounter_1 (
    .Clock(Clock), .Reset(Reset_out), .Adress(programcounter_1_adress));  // open: Adress__1
  RAM #(.addrWidth(16), .bus("separate"), .Select("low")) ram_1 (.addr(programcounter_1_adress));  // open: din, data, str, sel, clk, ld, clr

  // Notes on the sheet:
  //   16-BIT CPU
endmodule

module ProgramCounter (
  input  Clock,
  input  Reset,
  output [15:0] Adress,
  output [15:0] Adress__1
);

  Register_part #(.width(16), .Select("low")) register_1 (
    .D(Adress__1), .Q(Adress), .clk(Clock), .clr(Reset));  // open: en
  Adder #(.width(16)) adder_1 (.a(Adress), .b(16'h1), .out(Adress__1));  // open: cin, cout

  // Notes on the sheet:
  //   This module will point to an adress which executes the current instruction
endmodule

module InstructionDecode (
);


  // Notes on the sheet:
  //   This module translates each instruction and requests data and arithmetic inputs
endmodule

module ALU (
  input  Clock,
  input  [7:0] Instruction,
  input  [7:0] Data_A,
  input  [7:0] Data_AB,
  output [7:0] Output
);

  wire [7:0] adder_1_out, divider_1_out, multiplier_1_out, subtractor_1_out;

  Adder adder_1 (.a(Data_A), .b(Data_AB), .out(adder_1_out), .cin(Clock));  // open: cout
  Subtractor subtractor_1 (.a(Data_A), .b(Data_AB), .out(subtractor_1_out), .bin(Clock));  // open: bout
  Multiplier multiplier_1 (.a(Data_A), .b(Data_AB), .out(multiplier_1_out));  // open: cin, cout
  Divider divider_1 (.a(Data_A), .b(Data_AB), .out(divider_1_out));  // open: upper, rem
  Multiplexer #(.select(4), .width(8), .enable("false")) multiplexer_1 (
    .in0({8{1'b0}}), .in1(adder_1_out), .in3(subtractor_1_out), .in5(multiplier_1_out), .in7(divider_1_out),
    .out(Output), .sel(Instruction[3:0]));  // open: in2, in4, in6, in8, in9, in10, in11, in12, in13, in14, in15

  // Notes on the sheet:
  //   Instructions with registers only
endmodule

module Register (
  input  Clock,
  input  Reset,
  input  [7:0] Adress,
  input  [7:0] Adress_Output,
  input  [7:0] Data_A,
  output [7:0] out_6
);

  wire demultiplexer_2_out1, demultiplexer_2_out2, demultiplexer_2_out3, demultiplexer_2_out4,
       demultiplexer_2_out5, demultiplexer_2_out6, demultiplexer_2_out7, demultiplexer_2_out8,
       demultiplexer_2_out9, demultiplexer_2_out10, demultiplexer_2_out11, demultiplexer_2_out12,
       demultiplexer_2_out13, demultiplexer_2_out14, demultiplexer_2_out15;
  wire [7:0] demultiplexer_1_out1, demultiplexer_1_out2, demultiplexer_1_out3, demultiplexer_1_out4,
       demultiplexer_1_out5, demultiplexer_1_out6, demultiplexer_1_out7, demultiplexer_1_out8,
       demultiplexer_1_out9, demultiplexer_1_out10, demultiplexer_1_out11, demultiplexer_1_out12,
       demultiplexer_1_out13, demultiplexer_1_out14, demultiplexer_1_out15, register_1_q, register_2_q,
       register_3_q, register_5_q, register_6_q, register_7_q, register_8_q, register_9_q, register_10_q,
       register_11_q, register_12_q, register_13_q, register_14_q, register_15_q;

  Demultiplexer #(.select(4), .width(8), .enable("false")) demultiplexer_1 (
    .out1(demultiplexer_1_out1), .out2(demultiplexer_1_out2), .out3(demultiplexer_1_out3),
    .out4(demultiplexer_1_out4), .out5(demultiplexer_1_out5), .out6(demultiplexer_1_out6),
    .out7(demultiplexer_1_out7), .out8(demultiplexer_1_out8), .out9(demultiplexer_1_out9),
    .out10(demultiplexer_1_out10), .out11(demultiplexer_1_out11), .out12(demultiplexer_1_out12),
    .out13(demultiplexer_1_out13), .out14(demultiplexer_1_out14), .out15(demultiplexer_1_out15), .in(Data_A),
    .sel(Adress[3:0]));  // open: out0
  Demultiplexer #(.select(4), .enable("false")) demultiplexer_2 (
    .out1(demultiplexer_2_out1), .out2(demultiplexer_2_out2), .out3(demultiplexer_2_out3),
    .out4(demultiplexer_2_out4), .out5(demultiplexer_2_out5), .out6(demultiplexer_2_out6),
    .out7(demultiplexer_2_out7), .out8(demultiplexer_2_out8), .out9(demultiplexer_2_out9),
    .out10(demultiplexer_2_out10), .out11(demultiplexer_2_out11), .out12(demultiplexer_2_out12),
    .out13(demultiplexer_2_out13), .out14(demultiplexer_2_out14), .out15(demultiplexer_2_out15), .in(1'b1),
    .sel(Adress[3:0]));  // open: out0
  Register_part #(.Select("low")) register_1 (
    .D(demultiplexer_1_out1), .en(demultiplexer_2_out1), .Q(register_1_q), .clk(Clock), .clr(Reset));
  Register_part #(.Select("low")) register_2 (
    .D(demultiplexer_1_out2), .en(demultiplexer_2_out2), .Q(register_2_q), .clk(Clock), .clr(Reset));
  Register_part #(.Select("low")) register_3 (
    .D(demultiplexer_1_out3), .en(demultiplexer_2_out3), .Q(register_3_q), .clk(Clock), .clr(Reset));
  Register_part #(.Select("low")) register_4 (
    .D(demultiplexer_1_out4), .en(demultiplexer_2_out4), .Q(register_3_q), .clk(Clock), .clr(Reset));
  Register_part #(.Select("low")) register_5 (
    .D(demultiplexer_1_out5), .en(demultiplexer_2_out5), .Q(register_5_q), .clk(Clock), .clr(Reset));
  Register_part #(.Select("low")) register_6 (
    .D(demultiplexer_1_out6), .en(demultiplexer_2_out6), .Q(register_6_q), .clk(Clock), .clr(Reset));
  Register_part #(.Select("low")) register_7 (
    .D(demultiplexer_1_out7), .en(demultiplexer_2_out7), .Q(register_7_q), .clk(Clock), .clr(Reset));
  Register_part #(.Select("low")) register_8 (
    .D(demultiplexer_1_out8), .en(demultiplexer_2_out8), .Q(register_8_q), .clk(Clock), .clr(Reset));
  Register_part #(.Select("low")) register_9 (
    .D(demultiplexer_1_out9), .en(demultiplexer_2_out9), .Q(register_9_q), .clk(Clock), .clr(Reset));
  Register_part #(.Select("low")) register_10 (
    .D(demultiplexer_1_out10), .en(demultiplexer_2_out10), .Q(register_10_q), .clk(Clock), .clr(Reset));
  Register_part #(.Select("low")) register_11 (
    .D(demultiplexer_1_out11), .en(demultiplexer_2_out11), .Q(register_11_q), .clk(Clock), .clr(Reset));
  Register_part #(.Select("low")) register_12 (
    .D(demultiplexer_1_out12), .en(demultiplexer_2_out12), .Q(register_12_q), .clk(Clock), .clr(Reset));
  Register_part #(.Select("low")) register_13 (
    .D(demultiplexer_1_out13), .en(demultiplexer_2_out13), .Q(register_13_q), .clk(Clock), .clr(Reset));
  Register_part #(.Select("low")) register_14 (
    .D(demultiplexer_1_out14), .en(demultiplexer_2_out14), .Q(register_14_q), .clk(Clock), .clr(Reset));
  Register_part #(.Select("low")) register_15 (
    .D(demultiplexer_1_out15), .en(demultiplexer_2_out15), .Q(register_15_q), .clk(Clock), .clr(Reset));
  Multiplexer #(.select(4), .width(8), .enable("false")) multiplexer_1 (
    .in0({8{1'b0}}), .in1(register_1_q), .in2(register_2_q), .in3(register_3_q), .in4(register_3_q),
    .in5(register_5_q), .in6(register_6_q), .in7(register_7_q), .in8(register_8_q), .in9(register_9_q),
    .in10(register_10_q), .in11(register_11_q), .in12(register_12_q), .in13(register_13_q),
    .in14(register_14_q), .in15(register_15_q), .out(out_6), .sel(Adress_Output[3:0]));

  // Notes on the sheet:
  //   Register 1
endmodule
